# Fritzing sketch 6notGates (saved by Fritzing 0.9.4)
breadboards: 1

parts:
  U1 = SN74LS14N [package="DIP14 [THT]"]

nets:
  5V: U1.1A, U1.VCC
  N1: U1.1Y, U1.2A
  N2: U1.2Y, U1.3A
  N3: U1.3Y, U1.6A
  GND: U1.GND
  N4: U1.4A, U1.5Y
  N5: U1.5A, U1.6Y
