// Logisim project FA.circ as structural Verilog
module _4bit_adder_subtractor (
  input  c_in,
  input  a0,
  input  a1,
  input  a2,
  input  a3,
  input  b0,
  input  b1,
  input  b2,
  input  b3,
  output c0,
  output c1,
  output c2,
  output c3,
  output c_out
);

  wire n1bit_fa_1_c_out, n1bit_fa_2_c_out, n1bit_fa_3_c_out, xor_1_out, xor_2_out, xor_3_out, xor_4_out;

  xor xor_1 (xor_1_out, b0, c_in);
  xor xor_2 (xor_2_out, b1, c_in);
  xor xor_3 (xor_3_out, b2, c_in);
  xor xor_4 (xor_4_out, b3, c_in);
  _1bit_FA u_1bit_fa_1 (.a(a0), .b(xor_1_out), .c_in(c_in), .sum(c0), .c_out(n1bit_fa_1_c_out));
  _1bit_FA u_1bit_fa_2 (.a(a1), .b(xor_2_out), .c_in(n1bit_fa_1_c_out), .sum(c1), .c_out(n1bit_fa_2_c_out));
  _1bit_FA u_1bit_fa_3 (.a(a2), .b(xor_3_out), .c_in(n1bit_fa_2_c_out), .sum(c2), .c_out(n1bit_fa_3_c_out));
  _1bit_FA u_1bit_fa_4 (.a(a3), .b(xor_4_out), .c_in(n1bit_fa_3_c_out), .sum(c3), .c_out(c_out));
endmodule

module _1bit_FA (
  input  a,
  input  b,
  input  c_in,
  output sum,
  output c_out
);

  wire and_1_out, and_2_out, xor_1_out;

  xor xor_1 (xor_1_out, a, b);
  xor xor_2 (sum, xor_1_out, c_in);
  and and_1 (and_1_out, xor_1_out, c_in);
  and and_2 (and_2_out, a, b);
  or or_1 (c_out, and_1_out, and_2_out);
endmodule
